# Fritzing sketch Hardwareschema (saved by Fritzing 0.9.6b)
breadboards: 1

parts:
  Part1 = Adafruit BME680 [part_number="Adafruit #3660"]
  U1 = NodeMCU V1.0
  LED1 = RGB LED (com. cathode, rbg) [package="5 mm [THT]"]
  R1 = Resistor [tolerance=±5% power=0.25 resistance=220 package=THT]
  R2 = Resistor [tolerance=±5% power=0.25 resistance=220 package=THT]
  R3 = Resistor [tolerance=±5% power=0.25 resistance=220 package=THT]
  Part2 = Adafruit BME680 [part_number="Adafruit #3660"]  # not connected

nets:
  3.3V: Part1.3.3V, U1.3V3
  GND: Part1.GND, U1.GND, LED1.common_cathode
  N1: Part1.SCK/SCL, U1.D1
  N2: Part1.SDO/ADR, U1.D2
  N3: U1.D6, R2.Pin_0
  N4: U1.D7, R3.Pin_0
  N5: U1.D8, R1.Pin_0
  N6: LED1.red_anode, R1.Pin_1
  N7: LED1.blue_anode, R3.Pin_1
  N8: LED1.green_anode, R2.Pin_1

custom parts:
  NodeMCU V1.0: ESP8266 based NodeMCU
